# Fritzing sketch Carnifext Wiring (saved by Fritzing 0.9.6b)

parts:
  Part1 = Adafruit Prop Maker Wing [part_number=3988]
  D2F1 = D2F-FL Omron Snap Action Limit Switch with Level
  SP1 = SPEAKER [package=pcb_mount_speaker]  # not connected
  Part2 = Adafruit Breadboard-Friendly NeoPixel [part_number="Adafruit #1312"]
  Part3 = Adafruit Breadboard-Friendly NeoPixel [part_number="Adafruit #1312"]
  LED1 = RGB LED - (4 legs) [package="5 mm [THT]"]

nets:
  N1: Part1.SWITCH, D2F1.COM
  N2: Part1.GND, D2F1.NC
  GND: Part2.GND, Part3.GND, LED1.common_anode
  VDD: Part2.VDD, Part3.VDD, LED1.green_cathode
  N3: Part2.OUT, LED1.blue_cathode
  N4: Part3.IN, LED1.red_cathode

notes:
  Please refer to the Neopixel part page to identify the proper pinout for the through-hole Neopixel
  Mount this switch so that when teh trigger is pulled, it presses against the lever. You may want to bend the lever to allow a full range of motion while always having the trigger in contact with it

custom parts:
  Adafruit Prop Maker Wing: We’ve seen some great lightsaber builds and came up with a Wing just for prop makers! It has a class D amplifier for sound effects, can drive an 3 Watt RGB LED for bright lighting effects, has a built in accelerometer and a plug-n-play neopixel driver. We even made it easy to keep your prop running during all-day con’s with a power down pin to minimize current draw.
  D2F-FL Omron Snap Action Limit Switch with Level: Snap action switch with stainless steel lever.
  Adafruit Breadboard-Friendly NeoPixel: This is the easiest way possible to add small, bright RGB pixels to your project. We took the same technology from our Flora NeoPixels and made them breadboard friendly, with two rows of 3 x 0.1" spaced header on each side for easy soldering, chaining and breadboarding. These ultra-bright LEDs have a constant-current driver cooked right into the LED package! The pixels are chainable - so you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
